# Fritzing sketch TriMetricSerial (saved by Fritzing 0.9.3b)
breadboards: 1

parts:
  U1 = Voltage Regulator - 5V [package="TO220 [THT]"]
  Part1 = Arduino Uno (Rev3) - ICSP
  TM2030_J2 = RJ11 Jack [package=rj11-6]
  D1_1N4148 = Diode [package=diode-1n4148]
  D2_1N4148 = Diode [package=diode-1n4148]
  R1 = Resistor [tolerance=±5% resistance=47k package="0402 [SMD]"]
  R2 = Resistor [tolerance=±5% resistance=47k package="0402 [SMD]"]
  V1_-_From_TM2030_B1_&_G1 = DC Power [voltage=12V]

nets:
  N1: U1.input_voltage, V1_-_From_TM2030_B1_&_G1.V+
  GND: U1.GND, Part1.GND, V1_-_From_TM2030_B1_&_G1.V-
  N2: U1.output_voltage, Part1.5V, TM2030_J2.1, R1.Pin_0, R2.Pin_0
  N3: Part1.D2, D1_1N4148.A, R2.Pin_1
  N4: Part1.D4, D2_1N4148.A, R1.Pin_1
  N5: TM2030_J2.2, D1_1N4148.C
  N6: TM2030_J2.3, D2_1N4148.C

notes:
  12V
  (from TM2030 B1 & G1)
  COM-00107
